# Fritzing sketch Teensy_Capacitive_Touch_Sensing_XBee_IO_Line_Passing_Fritzing (saved by Fritzing 0.9.3b)
breadboards: 3

parts:
  Teensy_3_1 = Teensy 3.1
  Q1 = NPN-Transistor [package="TO92 [THT]"]
  R1 = Resistor [tolerance=±5% resistance=330 package="2010 [SMD]"]
  R2 = Resistor [tolerance=±5% resistance=10k package="2010 [SMD]"]
  Part2 = XBee Explorer Regulated
  S1 = Pushbutton [part_number=COM-09190 package="[THT]"]
  Q2 = NPN-Transistor [package="TO92 [THT]"]
  R3 = Resistor [tolerance=±5% resistance=220 package="2010 [SMD]"]
  Teensy1 = Teensy_3_1 XBee Adapter [part_number=13311]
  display1 = OpenSegment [part_number=COM-11644]
  JACK1 = 2.1mm Barrel Jack with Terminal Block

nets:
  GND: Teensy_3_1.GND, Q1.E, Teensy1.GND
  3V3: Teensy_3_1.3V3, R2.Pin_1, Teensy1.3.3V
  N1: Teensy_3_1.D13, R1.Pin_1, Teensy1.13/SCK
  N2: Q1.B, R1.Pin_0
  N3: Q1.C, R2.Pin_0, Teensy1.DIO0
  N4: Part2.GND, S1.Pin_3, S1.Pin_4, Q2.E, Q2.B, R3.Pin_0
  N5: Part2.DIO0, R3.Pin_1
  5V: Part2.5V, display1.VCC
  N6: S1.Pin_1, S1.Pin_2, display1.SDO
  N7: Q2.C, display1.SDI
  N8: display1.GND, JACK1.NEG
  N9: display1.RAW, JACK1.POS

notes:
  Copper Tape Electrode
  Transmitting Side
  Receiving Side
  Note: This is the back of Open Segment w/ Jumper for counter Closed
  Button to Decrement Counter by 1

custom parts:
  Pushbutton: A generic pushbutton. This is a standard 12mm square momentary button. What we really like is the large button head and good tactile feel (it ‘clicks’ really well). This button is great for user input on a PCB or a good, big reset button on a breadboard. Breadboard friendly! SparkFun Storefront SKU: COM-09190 Modified by: Ho Yun "Bobby" Chan @ SparkFun Electronics Inc.
  Teensy_3_1 XBee Adapter: The Teensy is an amazing development platform that allows you to get more computing power than an Arduino Uno, and in less space. The Teensy 3.1 XBee Adapter allows you to connect your Teensy with the tried and true XBee series to provide you with a great solution to any project that requires a decently ranged no-frills wireless serial link. Not only does the Teensy 3.1 XBee Adapter connect a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
  OpenSegment: Retired Product This product has been retired from our catalog and is no longer for sale. This page is made available for those looking for datasheets and the simply curious. OpenSegment makes it easy to add a large 7-segment display to your project. Because larger 7-segment displays pull more power than a microcontroller is able to drive directly, the OpenSegment has 8 PNP and 4 NPN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
